# Fritzing sketch section1_schematic (saved by Fritzing 0.9.3b)

parts:
  Part1 = Arduino Uno (Rev3)
  S1 = H-Bridge with L298N
  M1 = DC Motor
  M2 = DC Motor
  VCC1 = Battery
  Power_plug1 = Power plug
  U1 = SWITCH_SPDT [package=kps-1290]

nets:
  N1: Part1.D8, S1.IN1
  N2: Part1.D9_PWM, S1.IN2
  N3: Part1.D10_PWM/SS, S1.IN3
  N4: Part1.D11_PWM/MOSI, S1.IN4
  12V: S1.12V, Power_plug1.VCC, U1.P
  GND: S1.GND, VCC1.-, Power_plug1.GND
  N5: S1.ENA, S1.ENA-5V
  N6: S1.ENB, S1.ENB-5V
  N7: S1.M1-01, M1.pin_1
  N8: S1.M1-02, M1.pin_2
  N9: S1.M2-01, M2.pin_1
  N10: S1.M2-02, M2.pin_2
  N11: VCC1.+, U1.O

custom parts:
  H-Bridge with L298N: h-bridge
